// Logisim project control_logic.circ as structural Verilog: 1 circuit, main circuit control_logic
module control_logic (
  input  [31:0] inst,
  input  BrEq,
  input  BrLt,
  output PCSel,
  output RegWEn,
  output [2:0] ImmSel,
  output BrUn,
  output ASel,
  output BSel,
  output [3:0] ALUSel,
  output MemRW,
  output [1:0] WBSel
);

  Multiplexer #(.select(5), .width(4), .enable("false")) multiplexer_1 (
    .in0(4'b0000), .in1(4'b0110), .in3(4'b0111), .in4(4'b0011), .in5(4'b0100), .in6(4'b0010), .in7(4'b0001),
    .in8(4'b1010), .in9(4'b1110), .in11(4'b1011), .in13(4'b1000), .in15(4'b1001), .in16(4'b1100),
    .in21(4'b0101), .out(ALUSel), .sel({inst[30], inst[25], inst[14:12]}));  // open: in2, in10, in12, in14, in17, in18, in19, in20, in22, in23, in24, in25, in26, in27, in28, in29, in30, in31

  // Other names for the same wires on the sheet: func3[2:0] = inst[14:12]; func7[6:0] = inst[31:25];
  //   opcode[6:0] = inst[6:0]

  // Notes on the sheet:
  //   INPUTS to your circuit
  //   DON'T CHANGE THE LOCATIONS OF THE INPUTS AND OUTPUTS!
  //   OUTPUT from your circuit
endmodule
